# Fritzing sketch tp4 (saved by Fritzing 0.9.4)
breadboards: 1

parts:
  Composant1 = Arduino Uno (Rev3)
  R2 = Resistor [tolerance=±5% resistance=4.7k package=THT]
  R3 = Resistor [tolerance=±5% resistance=1k package=THT]
  R4 = Resistor [tolerance=±5% resistance=1k package=THT]

nets:
  N1: Composant1.A0, R2.Pin_1, R3.Pin_0
  N2: Composant1.GND, R3.Pin_1
  N3: R2.Pin_0, R4.Pin_1
